// Logisim project PC2.circ as structural Verilog: 2 circuits, main circuit main
module main (
);

  wire CLK, Reset;
  wire [4:0] instruction_decoder_1_rd, instruction_decoder_1_rs, instruction_decoder_1_rt,
       instruction_decoder_1_shamt;
  wire [5:0] instruction_decoder_1_funct, instruction_decoder_1_opcode;
  wire [15:0] instruction_decoder_1_immediate;
  wire [23:0] PC;
  wire [25:0] instruction_decoder_1_address;
  wire [31:0] adder_1_out, Curr_Inst, register_1_q;

  Clock clock_1 (.out(CLK));
  Button button_1 (.out(Reset));
  Register #(.width(32)) register_1 (.D(adder_1_out), .en(1'b1), .Q(register_1_q), .clk(CLK), .clr(Reset));
  Adder #(.width(32)) adder_1 (.a(32'h1), .b(register_1_q), .out(adder_1_out));  // open: cin, cout
  Bit_Extender #(.in_width(32), .out_width(24)) bit_extender_1 (.in(register_1_q), .out(PC));
  RAM #(.addrWidth(24), .dataWidth(32)) ram_1 (
    .addr(PC), .data(Curr_Inst), .sel(1'b1), .clk(CLK), .ld(1'b1), .clr(1'b0));
  Instruction_Decoder instruction_decoder_1 (
    .Inst(Curr_Inst), .Opcode(instruction_decoder_1_opcode), .rs(instruction_decoder_1_rs),
    .rt(instruction_decoder_1_rt), .rd(instruction_decoder_1_rd), .shamt(instruction_decoder_1_shamt),
    .funct(instruction_decoder_1_funct), .Immediate(instruction_decoder_1_immediate),
    .address(instruction_decoder_1_address));
  // Probe on instruction_decoder_1_opcode
  // Probe on instruction_decoder_1_rs
  // Probe on instruction_decoder_1_rt
  // Probe on instruction_decoder_1_rd
  // Probe on instruction_decoder_1_shamt
  // Probe on instruction_decoder_1_funct
  // Probe on instruction_decoder_1_immediate
  // Probe on instruction_decoder_1_address
  // Probe on PC
  // Probe on Curr_Inst

  // Notes on the sheet:
  //   Hex
endmodule

module Instruction_Decoder (
  input  [31:0] Inst,
  output [5:0] Opcode,
  output [4:0] rs,
  output [4:0] rt,
  output [4:0] rd,
  output [4:0] shamt,
  output [5:0] funct,
  output [15:0] Immediate,
  output [25:0] address
);


  assign address = Inst[25:0];
  assign funct = Inst[5:0];
  assign Immediate = Inst[15:0];
  assign Opcode = Inst[31:26];
  assign rd = Inst[15:11];
  assign rs = Inst[25:21];
  assign rt = Inst[20:16];
  assign shamt = Inst[10:6];
endmodule
